# Fritzing sketch Ph_10 (saved by Fritzing 0.9.9b)
breadboards: 1

parts:
  L1 = Inductor [package="400 mil [THT]"]
  R1 = Resistor [tolerance=±5% power=0.25 resistance=220 package=THT]
  S1 = Square Pushbutton
  U = Battery Holders [package=battery-aa-panel]
  R2 = Resistor [tolerance=±5% power=0.25 resistance=220 package=THT]
  LED1 = LEDs [package=led10mm]

nets:
  N1: L1.pin_0, S1.leg1, LED1.A
  N2: L1.pin_1, R2.Pin_0
  N3: R1.Pin_0, LED1.C
  N4: R1.Pin_1, R2.Pin_1
  N5: S1.leg0, U.+
